# Fritzing sketch Test 3 Schematic (saved by Fritzing 1.0.8)
breadboards: 1

parts:
  Time_of_Flight_Sensor = VL530X Time of Flight Distance Sensor [part_number="tonetoys #3317"]
  Arduino_Nano = Arduino Nano (Rev3.0)
  HC-SR04_Sensor_1 = HC-SR04 Ultrasonic Distance Sensor
  OLED_Display = Grove OLED 128x96
  IR_Obstacle_Avoidance_Sensor = fc-51 [package=THT]

nets:
  VCC: Time_of_Flight_Sensor.VCC, Arduino_Nano.5V, HC-SR04_Sensor_1.VCC, OLED_Display.VCC, IR_Obstacle_Avoidance_Sensor.pin3
  GND: Time_of_Flight_Sensor.GND, HC-SR04_Sensor_1.GND, IR_Obstacle_Avoidance_Sensor.pin2
  N1: Time_of_Flight_Sensor.SCL, Arduino_Nano.A5, OLED_Display.SCL
  N2: Time_of_Flight_Sensor.SDA, Arduino_Nano.A4, OLED_Display.SDA
  GND_2: Arduino_Nano.GND, OLED_Display.GND
  N3: Arduino_Nano.D4, HC-SR04_Sensor_1.TRIG
  N4: Arduino_Nano.D5, HC-SR04_Sensor_1.ECHO
  N5: Arduino_Nano.D8, IR_Obstacle_Avoidance_Sensor.pin1

custom parts:
  VL530X Time of Flight Distance Sensor: TOF
