# Fritzing sketch Test 4 Wiring Diagram (saved by Fritzing 1.0.8)
breadboards: 1

parts:
  Arduino_Nano = Arduino Nano (Rev3.0) (ICSP)
  TB6612_Motor_Controller = Adafruit TB6612 DC and Stepper Motor Driver [part_number="Adafruit #2448"]
  JACK1 = 2.1mm Barrel Jack with Terminal Block
  NEMA_17_Stepper_Motor = Stepper Motor - Bipolar
  Hall_Effect_Sensor = KY-003 Hall Magnetic Sensor Module [package="Breakout board"]
  MPU-6050_IMU = InvenSense MPU6050

nets:
  GND: Arduino_Nano.GND, TB6612_Motor_Controller.GND, JACK1.NEG, Hall_Effect_Sensor.-, MPU-6050_IMU.GND
  N1: Arduino_Nano.D4, TB6612_Motor_Controller.AIN2
  N2: Arduino_Nano.D5, TB6612_Motor_Controller.AIN1
  N3: Arduino_Nano.D6, TB6612_Motor_Controller.BIN1
  N4: Arduino_Nano.D7, TB6612_Motor_Controller.BIN2
  N5: Arduino_Nano.D10, Hall_Effect_Sensor.S
  VCC: Arduino_Nano.5V, TB6612_Motor_Controller.VCC, TB6612_Motor_Controller.PWMB, TB6612_Motor_Controller.STBY, TB6612_Motor_Controller.PWMA, Hall_Effect_Sensor.Vin, MPU-6050_IMU.VCC
  N6: Arduino_Nano.A5, MPU-6050_IMU.SCL
  N7: Arduino_Nano.A4, MPU-6050_IMU.SDA
  N8: TB6612_Motor_Controller.PWRIN, JACK1.POS
  N9: TB6612_Motor_Controller.MOTORA1, NEMA_17_Stepper_Motor.D
  N10: TB6612_Motor_Controller.MOTORA2, NEMA_17_Stepper_Motor.B
  N11: TB6612_Motor_Controller.MOTORB2, NEMA_17_Stepper_Motor.C
  N12: TB6612_Motor_Controller.MOTORB1, NEMA_17_Stepper_Motor.A

custom parts:
  KY-003 Hall Magnetic Sensor Module: KEYES KY-003 Arduino Hall Magnetic Sensor Module is a switch that will turn on/off in the presence of a magnetic field.
